# Fritzing sketch Particle_XYZ_Fritzing (saved by Fritzing 1.0.4)
breadboards: 1

parts:
  A1 = Particle - Photon2
  BAT1 = Battery Holders [package=lipo-1100mAh]  # not connected
  HC-SR04_Sensor_1 = HC-SR04 Ultrasonic Distance Sensor
  HC-SR04_Sensor_2 = HC-SR04 Ultrasonic Distance Sensor
  Part1 = BME280 Breakout

nets:
  VCC: A1.Pin_2, A1.Pin_31, HC-SR04_Sensor_2.VCC, Part1.3.3V
  GND: A1.Pin_4, A1.Pin_30, HC-SR04_Sensor_1.GND, HC-SR04_Sensor_2.GND, Part1.GND
  N1: A1.Pin_5, HC-SR04_Sensor_2.TRIG
  N2: A1.Pin_8, HC-SR04_Sensor_1.TRIG
  N3: A1.Pin_17, Part1.SDI/SDA
  N4: A1.Pin_18, Part1.SCK/SCL
  N5: A1.Pin_20, HC-SR04_Sensor_1.ECHO
  N6: A1.Pin_23, HC-SR04_Sensor_2.ECHO
  N7: A1.Pin_26, HC-SR04_Sensor_1.VCC

custom parts:
  Particle - Photon2: The Photon 2 is a microcontroller and Wi-Fi networking developed by particle. Features: 802.11a/b/g/n Wi-Fi, 2.4 GHz and 5 GHz Integrated PCB antenna Integrated U.FL connector for external antenna Integrated RF switch BLE 5 using same antenna as Wi-Fi Realtek RTL8721DM MCU ARM Cortex M33 CPU, 200 MHz 2048 KB (2 MB) user application maximum size 3072 KB (3 MB) of RAM available to user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
